// Logisim project pc.circ as structural Verilog
module Somador1bit (
  input  in_1,
  input  in_2,
  output out_3,
  output out_4
);

  xor xor_1 (out_3, in_1, in_2);
  and and_1 (out_4, in_1, in_2);
endmodule

module ULA (
  input  [15:0] A,
  input  [3:0] F,
  input  [15:0] B,
  input  [15:0] B_2,
  input  [15:0] A_2,
  input  [4:0] F_2,
  output [15:0] R,
  output [15:0] R_2
);

  wire not_1_out, not_2_out, not_3_out, not_4_out, not_5_out, or_1_out, or_2_out, or_3_out, or_4_out,
       or_5_out, or_6_out, or_7_out, or_8_out, or_9_out, or_10_out, or_11_out, or_12_out, or_13_out,
       or_14_out, or_15_out;
  wire [15:0] and_2_out, and_3_out, and_4_out, and_5_out, and_6_out, resltado_divisao, resultado_and,
       resultado_multicacao, resultado_or, resultado_soma, resultado_subtracao;
  wire [15:15] not_6_out, not_7_out, not_8_out, not_9_out, not_10_out;

  not not_1 (not_1_out, F[0]);
  or or_1 (or_1_out, F[2], F[3]);
  not not_2 (not_2_out, F[2]);
  or or_2 (or_2_out, not_2_out, F[3]);
  or or_3 (or_3_out, F[2], not_3_out);
  not not_3 (not_3_out, F[3]);
  not not_4 (not_4_out, F[0]);
  not not_5 (not_5_out, F[1]);
  or or_4 (or_4_out, F[2], F[3]);
  or or_5 (or_5_out, F[0], F[1]);
  or or_6 (or_6_out, or_5_out, or_7_out);
  or or_7 (or_7_out, F[2], F[3]);
  or or_8 (or_8_out, not_1_out, F[1]);
  or or_9 (or_9_out, or_8_out, or_1_out);
  or or_10 (or_10_out, F[0], F[1]);
  or or_11 (or_11_out, or_10_out, or_2_out);
  or or_12 (or_12_out, F[0], F[1]);
  or or_13 (or_13_out, or_12_out, or_3_out);
  or or_14 (or_14_out, not_4_out, not_5_out);
  or or_15 (or_15_out, or_14_out, or_4_out);
  not not_6 (not_6_out[15], or_6_out);
  not not_7 (not_7_out[15], or_9_out);
  not not_8 (not_8_out[15], or_11_out);
  not not_9 (not_9_out[15], or_13_out);
  not not_10 (not_10_out[15], or_15_out);
  Adder #(.width(16)) adder_1 (.a(A), .b(B), .out(resultado_soma));  // open: cin, cout
  Subtractor #(.width(16)) subtractor_1 (.a(A), .b(B), .out(resultado_subtracao));  // open: bin, bout
  Multiplier #(.width(16)) multiplier_1 (.a(A), .b(B), .out(resultado_multicacao));  // open: cin, cout
  Divider #(.width(16)) divider_1 (.a(A), .b(B), .out(resltado_divisao));  // open: upper, rem
  assign resultado_and = A & B;  // AND_Gate and_1, 16 bits wide
  assign resultado_or = A | B;  // OR_Gate or_16, 16 bits wide
  assign and_2_out = {16{not_6_out[15]}} & resultado_soma;  // AND_Gate and_2, 16 bits wide
  assign and_3_out = {16{not_7_out[15]}} & resultado_subtracao;  // AND_Gate and_3, 16 bits wide
  assign and_4_out = {16{not_8_out[15]}} & resultado_multicacao;  // AND_Gate and_4, 16 bits wide
  assign and_5_out = {16{not_9_out[15]}} & resltado_divisao;  // AND_Gate and_5, 16 bits wide
  assign and_6_out = {16{not_10_out[15]}} & resultado_and;  // AND_Gate and_6, 16 bits wide
  assign R = and_2_out | and_3_out | and_4_out | and_5_out | and_6_out;  // OR_Gate or_17, 16 bits wide
  Shifter #(.width(16)) shifter_1 ();  // open: in, dist, out
  Shifter #(.width(16), .shift("lr")) shifter_2 ();  // open: in, dist, out
  Comparator #(.width(16), .mode("unsigned")) comparator_1 ();  // open: a, b, gt, eq, lt
  // NOT_Gate not_11 is placed but not wired
  Multiplexer #(.select(5), .width(16)) multiplexer_1 (
    .in0(B_2), .in1(A_2), .out(R_2), .sel(F_2));  // open: in2, in3, in4, in5, in6, in7, in8, in9, in10, in11, in12, in13, in14, in15, in16, in17, in18, in19, in20, in21, in22, in23, in24, in25, in26, in27, in28, in29, in30, in31, en

  // Other names for the same wires on the sheet: b0 = F[0]; b1 = F[1]; b2 = F[2]; b3 = F[3]
endmodule
